# Fritzing sketch RCM twoside PCB 2 (saved by Fritzing 0.9.3b)
circuit board: 6.9cm x 5cm

parts:
  J3 = female pin header, 2 pins [form="♀ (female)"]
  J4 = female pin header, 2 pins [form="♀ (female)"]
  J7 = female pin header, 2 pins [form="♀ (female)"]
  J8 = female pin header, 2 pins [form="♀ (female)"]
  J9 = male pin header, 6 pins [form="♂ (male)"]
  J11 = male pin header, 5 pins [form="♂ (male)"]
  R2 = Resistor [tolerance=±5% resistance=10k package=THT]
  C1 = Tantalum Capacitor [capacitance=47µF package="100 mil [THT, tantalum]"]
  J10 = male pin header, 6 pins [form="♂ (male)"]
  R1 = Resistor [tolerance=±5% resistance=5k package=THT]
  J1 = female pin header, 2 pins [form="♀ (female)"]
  J2 = female pin header, 2 pins [form="♀ (female)"]
  J6 = female pin header, 2 pins [form="♀ (female)"]
  IC2 = L293D [package=THT]
  J5 = female pin header, 2 pins [form="♀ (female)"]
  IC1 = L293D [package=THT]
  U1 = ESP32S-HiLetgo [part_number=ESP32S-HiLetgo]
  J12 = male pin header, 12 pins [form="♂ (male)"]

nets:
  N1: J3.pin1, J3.pin2, IC1.Out_4_(_Controlled_by_Enable_2_)
  N2: J4.pin1, J4.pin2, IC1.Out_3_(_Controlled_by_Enable_2_)
  N3: J7.pin1, J7.pin2, IC1.Out_2_(_Controlled_by_Enable_1_)
  N4: J8.pin1, J8.pin2, IC1.Out_1_(_Controlled_by_Enable_1_)
  N5: J9.pin1, J9.pin2, J9.pin3, J9.pin4, J9.pin5, J9.pin6, C1.-, R1.Pin_1, IC2.0V, IC1.0V, U1.GND, J12.pin1, J12.pin2
  N6: J11.pin1, U1.GPIO27, J12.pin12
  N7: J11.pin2, U1.GPIO26, J12.pin11
  N8: J11.pin3, U1.GPIO25, J12.pin10
  N9: J11.pin4, U1.GPIO33, J12.pin9
  N10: J11.pin5, U1.GPIO32, J12.pin8
  N11: R2.Pin_0, C1.+, J10.pin1, J10.pin2, J10.pin3, J10.pin4, J10.pin5, J10.pin6, IC2.+Vmotor, IC2.+V, IC1.+Vmotor, IC1.+V, U1.VIN
  N12: R2.Pin_1, R1.Pin_0, U1.GPIO36
  N13: J1.pin1, J1.pin2, IC2.Out_4_(_Controlled_by_Enable_2_)
  N14: J2.pin1, J2.pin2, IC2.Out_3_(_Controlled_by_Enable_2_)
  N15: J6.pin1, J6.pin2, IC2.Out_1_(_Controlled_by_Enable_1_)
  N16: IC2.Enable_1, U1.GPIO17
  N17: IC2.In_1, U1.GPIO16
  N18: IC2.Out_2_(_Controlled_by_Enable_1_), J5.pin1, J5.pin2
  N19: IC2.In_2, U1.GPIO12
  N20: IC2.Enable_2, U1.GPIO13
  N21: IC2.In_3, U1.GPIO4
  N22: IC2.In_4, U1.GPIO14
  N23: IC1.Enable_1, U1.GPIO23
  N24: IC1.In_1, U1.GPIO22
  N25: IC1.In_2, U1.GPIO19
  N26: IC1.Enable_2, U1.GPIO5
  N27: IC1.In_3, U1.GPIO18
  N28: IC1.In_4, U1.GPIO21
  N29: U1.3.3, J12.pin3, J12.pin4
  N30: U1.GPIO39, J12.pin5
  N31: U1.GPIO34, J12.pin6
  N32: U1.GPIO35, J12.pin7

notes:
  RCM
  USB
  <-
  -+
  5
  1
  A
  B
  C
  D
  not really
  47uF
  10K
  5K
  2
  3
  4

custom parts:
  ESP32S-HiLetgo: HiLetgo ESP-WROOM-32 ESP32 ESP-32S Development Board 2.4GHz Dual-Mode WiFi + Bluetooth Dual Cores Microcontroller The ESP32 integrated with Antenna switches, RF Balun, power amplifiers, low-noise amplifiers, filters, and management modules, and the entire solution occupies the least area of PCB. 2.4 GHz Wi-Fi plus Bluetooth dual-mode chip, with TSMC Ultra-low power consumption 40nm technology,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
